# Fritzing sketch breadboard-example (saved by Fritzing 0.9.3b)
breadboards: 1

parts:
  Bauteil1 = Photon
  GND = XLR NC3MAAH [package=nc3maah]
  R1 = Resistor [tolerance=±5% resistance=100 package=THT]  # not connected
  IC1 = IC, DIP package, 8 pins [chip_label=IC]

nets:
  N1: Bauteil1.TX, IC1.pin4
  N2: Bauteil1.GND, GND.1, GND.G, IC1.pin1
  N3: Bauteil1.VIN, IC1.pin2, IC1.pin3, IC1.pin8
  N4: GND.2, IC1.pin7
  N5: GND.3, IC1.pin6

notes:
  GND
  3 DMX+
  2 DMX-
  1 GND
